// Logisim project 4BitMIPS.circ as structural Verilog: 1 circuit, main circuit 4 Bit MIPS
module _4_Bit_MIPS (
  output [7:0] out_1,
  output [7:0] out_2,
  output [2:0] out_3,
  output [3:0] out_4,
  output [3:0] out_5,
  output [3:0] out_6,
  output [3:0] out_7,
  output [7:0] out_8,
  output [3:0] out_9,
  output [3:0] out_10,
  output [3:0] out_11,
  output [3:0] out_12,
  output [3:0] out_13,
  output [3:0] out_14
);

  wire clock_1_out, control_unit_1_alu_src, control_unit_1_bneq, control_unit_1_branch, control_unit_1_jump,
       control_unit_1_memread, control_unit_1_memtoreg, control_unit_1_memwrite, control_unit_1_reg_dst,
       control_unit_1_regwrite, n4bitalu_1_zero, n7408_1_p3, n7486_1_p5, register_1_p10, register_1_p17;
  wire [3:0] data_memory_1_out, instruction_memory_1_output_0, instruction_memory_1_output_1,
       instruction_memory_1_output_2, instruction_memory_1_output_3, n4bit_mux_1_y, n4bitalu_1_output,
       register_1_p5;
  wire [7:0] adder_1_out, adder_2_out, n8bitmux_1_f, sp_extender_1_out_3;

  Clock clock_1 (.out(clock_1_out));
  Instruction_Memory instruction_memory_1 (
    .Output_0(instruction_memory_1_output_0), .Output_1(instruction_memory_1_output_1),
    .Output_2(instruction_memory_1_output_2), .Output_3(instruction_memory_1_output_3), .PC(out_8),
    .CLK(clock_1_out), .PC_2(out_2));
  Adder adder_1 (.a(out_2), .b(8'h1), .out(adder_1_out), .cin(1'b0));  // open: cout
  Sign_Extender_main main_1 (._4_Bit(instruction_memory_1_output_0), ._8_bit(out_1));
  _4BIT_MUX u_4bit_mux_1 (
    .A(instruction_memory_1_output_1), .B(instruction_memory_1_output_0), .S(control_unit_1_reg_dst),
    .Y(n4bit_mux_1_y));
  Control_Unit control_unit_1 (
    .OPCode(instruction_memory_1_output_3), .JUMP(control_unit_1_jump), .BNEQ(control_unit_1_bneq),
    .RegWrite(control_unit_1_regwrite), .ALU_SRC(control_unit_1_alu_src), .ALU_OP(out_3),
    .MemToReg(control_unit_1_memtoreg), .MemWrite(control_unit_1_memwrite), .MemRead(control_unit_1_memread),
    .BRANCH(control_unit_1_branch), .REG_DST(control_unit_1_reg_dst));  // open: out_2, ALU0, ALU1, ALU2
  // Register register_1: pin names not known; wires that end beside it: instruction_memory_1_output_2, instruction_memory_1_output_1, clock_1_out, n4bit_mux_1_y, register_1_p5, control_unit_1_regwrite, out_9, out_10, out_11, register_1_p10, out_12, register_1_p10, out_13, out_14, out_4, out_7, register_1_p17
  _4BIT_MUX u_4bit_mux_2 (.A(out_7), .B(instruction_memory_1_output_0), .S(control_unit_1_alu_src), .Y(out_5));
  _4BitALU u_4bitalu_1 (
    .A(out_4), .B(out_5), .ALU_OpCode(out_3), .Output(n4bitalu_1_output), .Zero(n4bitalu_1_zero));  // open: Overflow
  Adder adder_2 (.a(adder_1_out), .b(out_1), .out(adder_2_out), .cin(1'b0));  // open: cout
  sp_extender sp_extender_1 (.in_1(n4bitalu_1_output), .in_2(register_1_p17), .out_3(sp_extender_1_out_3));
  Data_Memory data_memory_1 (
    .Address(sp_extender_1_out_3), .Write_Data(out_7), .MemWrite(control_unit_1_memwrite),
    .MemRead(control_unit_1_memread), .out(data_memory_1_out), .CLK(clock_1_out));
  _8BitMux u_8bitmux_1 (.A(adder_1_out), .B(adder_2_out), .S(n7408_1_p3), .F(n8bitmux_1_f));
  // _7486 7486_1: pin names not known; wires that end beside it: 1'b0, 1'b1, control_unit_1_bneq, n4bitalu_1_zero, n7486_1_p5
  _4BIT_MUX u_4bit_mux_3 (.A(n4bitalu_1_output), .B(data_memory_1_out), .S(control_unit_1_memtoreg), .Y(register_1_p5));
  _8BitMux u_8bitmux_2 (
    .A(n8bitmux_1_f), .B({instruction_memory_1_output_2, instruction_memory_1_output_1}),
    .S(control_unit_1_jump), .F(out_8));
  // _7408 7408_1: pin names not known; wires that end beside it: n7486_1_p5, control_unit_1_branch, n7408_1_p3, 1'b0, 1'b1

  assign out_6 = out_4;
endmodule
