// Logisim project 4bitALU.circ as structural Verilog: 1 circuit, main circuit 4BitALU
// 2
module _4BitALU (
  input  [3:0] A,
  input  [3:0] B,
  input  [2:0] ALU_OpCode,
  input  [3:0] in_4,
  output Overflow,
  output Zero,
  output [3:0] Output
);

  wire adder_1_cout, subtractor_1_bout;
  wire [3:0] adder_1_out, and_1_out, nor_1_out, or_1_out, shifter_1_out, shifter_2_out, subtractor_1_out;

  Adder #(.width(4)) adder_1 (.a(A), .b(B), .out(adder_1_out), .cin(1'b0), .cout(adder_1_cout));
  Subtractor #(.width(4)) subtractor_1 (.a(A), .b(B), .out(subtractor_1_out), .bin(1'b0), .bout(subtractor_1_bout));
  assign or_1_out = A | B;  // OR_Gate or_1, 4 bits wide
  assign and_1_out = A & B;  // AND_Gate and_1, 4 bits wide
  Shifter #(.width(4)) shifter_1 (.in(A), .\dist (B[1:0]), .out(shifter_1_out));
  Shifter #(.width(4), .shift("lr")) shifter_2 (.in(A), .\dist (B[1:0]), .out(shifter_2_out));
  assign nor_1_out = ~(A | B);  // NOR_Gate nor_1, 4 bits wide
  Multiplexer #(.select(3)) multiplexer_1 (
    .in0(adder_1_cout), .in1(subtractor_1_bout), .in2(1'b0), .in3(1'b0), .in4(1'b0), .in5(1'b0), .in6(1'b0),
    .in7(1'b0), .out(Overflow), .sel(ALU_OpCode));  // open: en
  Multiplexer #(.select(3), .width(4)) multiplexer_2 (
    .in0(adder_1_out), .in1(subtractor_1_out), .in2(or_1_out), .in3(and_1_out), .in4(nor_1_out),
    .in5(shifter_1_out), .in6(shifter_2_out), .out(Output), .sel(ALU_OpCode));  // open: in7, en
  Comparator #(.width(4)) comparator_1 (.a(Output), .b(in_4), .eq(Zero));  // open: gt, lt
endmodule
