// Logisim project ControlUnit.circ as structural Verilog: 1 circuit, main circuit Control Unit
module Control_Unit (
  input  [3:0] OPCode,
  output [11:0] out_2,
  output JUMP,
  output BNEQ,
  output RegWrite,
  output ALU_SRC,
  output ALU0,
  output ALU1,
  output ALU2,
  output [2:0] ALU_OP,
  output MemToReg,
  output MemWrite,
  output MemRead,
  output BRANCH,
  output REG_DST
);

  ROM #(.addrWidth(4), .dataWidth(12)) rom_1 (
    .addr(OPCode),
    .data({out_2[11], BRANCH, MemRead, MemWrite, MemToReg, ALU2, ALU1, ALU0, ALU_SRC, out_2[2], BNEQ, JUMP}),
    .sel(1'b1));

  assign ALU_OP = {ALU2, ALU1, ALU0};
  assign {out_2[10:3], out_2[1:0]} = {BRANCH, MemRead, MemWrite, MemToReg, ALU2, ALU1, ALU0, ALU_SRC, BNEQ, JUMP};
  assign REG_DST = out_2[11];
  assign RegWrite = out_2[2];

  // Notes on the sheet:
  //   contents of rom_1 (hex, n*v repeats v):
  //   414 800 840 820 008 058 10c 810 005 830 068 028 416 018 038 288
endmodule
