// Logisim project Data Memory.circ as structural Verilog: 1 circuit, main circuit Data Memory
module Data_Memory (
  input  [3:0] Address,
  input  [3:0] Write_Data,
  input  MemWrite,
  input  MemRead,
  output [11:0] out_5,
  output [3:0] Read_Data,
  output out_7,
  output out_8,
  output out_9,
  output out_10,
  output out_11,
  output out_12,
  output out_13,
  output out_14,
  output out_15,
  output out_16,
  output out_17,
  output out_18
);

  ROM #(.addrWidth(4), .dataWidth(12)) rom_1 (.addr(Address), .data(out_5), .sel(1'b1));

  assign out_7 = out_5[0];
  assign out_8 = out_5[1];
  assign out_9 = out_5[2];
  assign out_10 = out_5[3];
  assign out_11 = out_5[4];
  assign out_12 = out_5[5];
  assign out_13 = out_5[6];
  assign out_14 = out_5[7];
  assign out_15 = out_5[8];
  assign out_16 = out_5[9];
  assign out_17 = out_5[10];
  assign out_18 = out_5[11];

  // Notes on the sheet:
  //   contents of rom_1 (hex, n*v repeats v):
  //   410 804 844 824 c 5c 108 814 1 834 6c 2c 412 1c 3c 28c
endmodule
