// Logisim project Instruction Memory.circ as structural Verilog: 1 circuit, main circuit Instruction Memory
module Instruction_Memory (
  input  [7:0] PC,
  input  CLK,
  output [7:0] PC_2,
  output [3:0] Output_0,
  output [3:0] Output_1,
  output [3:0] Output_2,
  output [3:0] Output_3
);

  Register register_1 (.D(PC), .en(1'b1), .Q(PC_2), .clk(CLK), .clr(1'b0));
  ROM #(.dataWidth(16)) rom_1 (.addr(PC_2), .data({Output_3, Output_2, Output_1, Output_0}), .sel(1'b1));

  // Notes on the sheet:
  //   contents of rom_1 (hex, n*v repeats v):
  //   4021 4032 1244 13*0 dfa1 7*0 ad
endmodule
