// Logisim project MUX.circ as structural Verilog: 3 circuits, main circuit 4BIT MUX
module _4BIT_MUX (
  input  [3:0] A,
  input  [3:0] B,
  input  S,
  output [3:0] Y
);

  // _74157 74157_1: pin names not known; wires that end beside it: S, A[0], B[0], Y[0], A[1], B[1], Y[1], 1'b0, 1'b1, 1'b0, A[3], B[3], Y[3], A[2], B[2], Y[2]
endmodule

module _7_4__TO_1_4__MUX (
  input  [3:0] in_1,
  input  [3:0] in_2,
  input  [3:0] in_3,
  input  [3:0] in_4,
  input  [3:0] in_5,
  input  [3:0] in_6,
  input  [3:0] in_7,
  input  [3:0] in_8,
  output [3:0] out_9
);

  wire [3:0] n4bit_mux_1_y, n4bit_mux_2_y, n4bit_mux_3_y, n4bit_mux_4_y, n4bit_mux_5_y, n4bit_mux_6_y;

  _4BIT_MUX u_4bit_mux_1 (.A(in_1), .B(in_2), .S(in_6[0]), .Y(n4bit_mux_1_y));
  _4BIT_MUX u_4bit_mux_2 (.A(in_3), .B(in_4), .S(in_6[0]), .Y(n4bit_mux_2_y));
  _4BIT_MUX u_4bit_mux_3 (.A(in_5), .B(in_7), .S(in_6[0]), .Y(n4bit_mux_3_y));
  _4BIT_MUX u_4bit_mux_4 (.A(in_8), .B(4'b0000), .S(in_6[0]), .Y(n4bit_mux_4_y));
  _4BIT_MUX u_4bit_mux_5 (.A(n4bit_mux_1_y), .B(n4bit_mux_2_y), .S(in_6[1]), .Y(n4bit_mux_5_y));
  _4BIT_MUX u_4bit_mux_6 (.A(n4bit_mux_3_y), .B(n4bit_mux_4_y), .S(in_6[1]), .Y(n4bit_mux_6_y));
  _4BIT_MUX u_4bit_mux_7 (.A(n4bit_mux_5_y), .B(n4bit_mux_6_y), .S(in_6[2]), .Y(out_9));
endmodule

module _8BitMux (
  input  [7:0] A,
  input  [7:0] B,
  input  S,
  output [7:0] F
);

  _4BIT_MUX u_4bit_mux_1 (.A(A[3:0]), .B(B[3:0]), .S(S), .Y(F[3:0]));
  _4BIT_MUX u_4bit_mux_2 (.A(A[7:4]), .B(B[7:4]), .S(S), .Y(F[7:4]));
endmodule
