// Logisim project Register File.circ as structural Verilog: 1 circuit, main circuit Register
module Register (
  input  [3:0] Write_Data,
  input  [3:0] Write_Reg,
  input  CLK,
  input  Reg_Write,
  input  [3:0] Read_Reg_1,
  input  [3:0] Read_Reg_2,
  output [3:0] sp,
  output [3:0] t0,
  output [3:0] t1,
  output [3:0] t2,
  output [3:0] t3,
  output [3:0] t4,
  output [3:0] Read_Data_1,
  output [3:0] Read_Data_2,
  output isSp
);

  wire n7404_1_p2, n7404_1_p4, n7404_1_p6, n7404_1_p10, n7404_1_p12, n7404_1_p14, n74138_1_p9, n74138_1_p10,
       n74138_1_p11, n74138_1_p12, n74138_1_p13, n74138_1_p14;
  wire [3:0] Zero_q;

  Register_part #(.width(4)) Zero (.en(1'b0), .Q(Zero_q), .clk(CLK), .clr(1'b1));  // open: D
  // _74138 74138_1: pin names not known; wires that end beside it: Write_Reg[0], Write_Reg[1], Write_Reg[2], Write_Reg[3], Reg_Write, 1'b1, 1'b0, 1'b1, n74138_1_p9, n74138_1_p10, n74138_1_p11, n74138_1_p12, n74138_1_p13, n74138_1_p14
  // _7404 7404_1: pin names not known; wires that end beside it: n74138_1_p12, n7404_1_p2, n74138_1_p13, n7404_1_p4, n74138_1_p14, n7404_1_p6, 1'b0, 1'b1, n74138_1_p9, n7404_1_p10, n74138_1_p10, n7404_1_p12, n74138_1_p11, n7404_1_p14
  Register_part #(.width(4)) u_t0 (.D(Write_Data), .en(n7404_1_p10), .Q(t0), .clk(CLK), .clr(1'b0));
  Register_part #(.width(4)) u_t1 (.D(Write_Data), .en(n7404_1_p12), .Q(t1), .clk(CLK), .clr(1'b0));
  Register_part #(.width(4)) u_t2 (.D(Write_Data), .en(n7404_1_p14), .Q(t2), .clk(CLK), .clr(1'b0));
  Register_part #(.width(4)) u_t3 (.D(Write_Data), .en(n7404_1_p2), .Q(t3), .clk(CLK), .clr(1'b0));
  Register_part #(.width(4)) u_t4 (.D(Write_Data), .en(n7404_1_p4), .Q(t4), .clk(CLK), .clr(1'b0));
  Register_part #(.width(4)) u_sp (.D(Write_Data), .en(n7404_1_p6), .Q(sp), .clk(CLK), .clr(1'b0));
  _7_4__TO_1_4__MUX u_7_4_to_1_4_mux_1 (
    .in_1(Zero_q), .in_2(t0), .in_3(t1), .in_4(t2), .in_5(t3), .in_6(Read_Reg_1), .in_7(t4), .in_8(sp),
    .out_9(Read_Data_1));
  _7_4__TO_1_4__MUX u_7_4_to_1_4_mux_2 (
    .in_1(Zero_q), .in_2(t0), .in_3(t1), .in_4(t2), .in_5(t3), .in_6(Read_Reg_2), .in_7(t4), .in_8(sp),
    .out_9(Read_Data_2));
  Comparator #(.width(4)) comparator_1 (.a(Read_Reg_1), .b(4'b0110), .eq(isSp));  // open: gt, lt
endmodule
