// Logisim project Sign Extender.circ as structural Verilog: 2 circuits, main circuit main
module main (
  input  [3:0] _4_Bit,
  output [7:0] _8_bit
);


  assign _8_bit = {{5{_4_Bit[3]}}, _4_Bit[2:0]};
endmodule

module sp_extender (
  input  [3:0] in_1,
  input  in_2,
  output [7:0] out_3
);


  assign out_3 = {1'b0, in_2, 2'b00, in_1};
endmodule
