// Logisim project data memory.circ as structural Verilog: 1 circuit, main circuit Data Memory
module Data_Memory (
  input  [7:0] Address,
  input  [3:0] Write_Data,
  input  CLK,
  input  MemWrite,
  input  MemRead,
  output [3:0] out
);

  RAM #(.dataWidth(4), .bus("separate")) ram_1 (
    .addr(Address), .din(Write_Data), .data(out), .str(MemWrite), .sel(1'b1), .clk(CLK), .ld(MemRead),
    .clr(1'b0));
endmodule
